// Logisim project 8bitlogism (1).circ as structural Verilog: 1 circuit, main circuit main
module main (
  input  [7:0] in_1,
  input  [7:0] in_2,
  input  [2:0] OP_CODE,
  output [7:0] OUTPUT
);

  wire [7:0] adder_1_out, and_1_out, multiplexer_1_out, not_1_out, or_1_out, subtractor_1_out, undriven,
       xor_1_out;

  assign not_1_out = ~in_1;  // NOT_Gate not_1, 8 bits wide
  assign or_1_out = in_1 | in_2;  // OR_Gate or_1, 8 bits wide
  assign xor_1_out = in_1 ^ in_2;  // XOR_Gate xor_1, 8 bits wide
  assign and_1_out = in_1 & in_2;  // AND_Gate and_1, 8 bits wide
  Multiplexer #(.select(2), .width(8)) multiplexer_1 (
    .in0(in_1), .in3(in_2), .out(multiplexer_1_out));  // open: in1, in2, sel, en
  Adder adder_1 (.a(in_1), .b(in_2), .out(adder_1_out));  // open: cin, cout
  Subtractor subtractor_1 (.a(in_1), .b(in_2), .out(subtractor_1_out));  // open: bin, bout
  // Buffer buffer_1 has open pins: in=undriven, out=open
  Multiplexer #(.select(3), .width(8)) multiplexer_2 (
    .in0(not_1_out), .in1(or_1_out), .in2(xor_1_out), .in3(and_1_out), .in4(multiplexer_1_out),
    .in5(adder_1_out), .in6(subtractor_1_out), .in7(undriven), .out(OUTPUT), .sel(OP_CODE));  // open: en

  // Notes on the sheet:
  //   OR
  //   XOR
  //   AND
  //   4X4
  //   MUX
  //   8-BIT
  //   ADDER
  //   8-BIT
  //   SUBTRACTOR
  //   8-TO-1
  //   MULTIPLEXER
endmodule
