// Logisim project ALU (2).circ as structural Verilog: 1 circuit, main circuit main
module main (
  input  A,
  input  B,
  input  C,
  input  D,
  input  [1:0] in_5,
  output out_6,
  output Cout
);

  wire adder_1_out, and_1_out, or_1_out, xor_1_out;

  and and_1 (and_1_out, A, B);
  or or_1 (or_1_out, A, B);
  xor xor_1 (xor_1_out, B, D);
  Adder #(.width(1)) adder_1 (.a(A), .b(xor_1_out), .out(adder_1_out), .cin(C), .cout(Cout));
  Multiplexer #(.select(2)) multiplexer_1 (
    .in1(and_1_out), .in2(or_1_out), .in3(adder_1_out), .out(out_6), .sel(in_5));  // open: in0, en
endmodule
